# Fritzing sketch schema (saved by Fritzing 0.9.4)

parts:
  U1 = LuaNode32 / ESP32
  Součástka1 = Solar Cell
  Součástka2 = INA219 High Side DC Current Sensor Breakout [part_number=904]
  U4 = MPC1700 [package=sot23-3]
  C2 = Electrolytic Capacitor [capacitance=1000μF package="1010 [SMD, electrolytic]"]
  C3 = Capacitor [package=cap-pth-small2]
  Součástka10 = GY-BMEP280 Barometric Pressure Sensor - Breakout
  Part1 = Solar Charge Controller [part_number="HGX Series Solar Charge Controller PWM" package=PWM-Model]
  VCC1 = Battery block 9V
  Součástka14 = INA219 High Side DC Current Sensor Breakout [part_number=904]
  M1 = INA3221 Triple Channel Current/Voltage Monitor Module [part_number="3221 Black"]  # not connected

nets:
  GND: U1.GND, Součástka2.GND, U4.GND, C2.-, C3.1, Součástka10.GND, Part1.Connector_6, Součástka14.GND
  VCC: U1.3V3, Součástka2.VCC, U4.OUT, Součástka10.VCC, Součástka14.VCC
  N1: U1.D21, Součástka1.+, Součástka2.VIN+, Součástka2.SDA, Součástka10.SDA, Part1.Connector_3, Součástka14.VIN-, Součástka14.SDA
  N2: U1.TX0, U1.D22, Součástka2.VIN-, Součástka2.SCL, Součástka10.SCL, Part1.Connector_1, Součástka14.SCL
  N3: Součástka1.-, Part1.Connector_2
  N4: U4.IN, C2.+, C3.2, Part1.Connector_5
  N5: Part1.Connector_4, VCC1.-
  N6: VCC1.+, Součástka14.VIN+

notes:
  MAX4466 MIC sensors
  vin, gnd, scl, sda, temp addr, gyro addr, mic vin, mic out
  18V 40W solar panel
  12V 55Ah battery
  12V -> 3.3V
  Magnetic lock sensors
  MMA8452Q gyroscope sensors
  INA219 sensors
  SHT31 temperature/humidity sensors
  BMP280 temperature/humidity/presure sensor

custom parts:
  LuaNode32 / ESP32: ESP32 based LuaNode32
  INA219 High Side DC Current Sensor Breakout: This breakout board will solve all your power-monitoring problems. Instead of struggling with two multimeters, you can just use the handy INA219B chip on this breakout to both measure both the high side voltage and DC current draw over I2C with 1% precision. Most current-measuring devices such as our current panel meter are only good for low side measuring. That means that unless you want to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
  MPC1700: Small package LDO
  GY-BMEP280 Barometric Pressure Sensor - Breakout: The BME280 is a chip which was originally designed for the next generation of smartphones. It is made up of a very accurate pressure sensor and an associated temperature sensor which helps calibrate the pressure readings. And just for fun they threw in a pretty solid humidity sensor in there as well! So with an I2C connection you have access to enough weather data to make some pretty good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
  Solar Charge Controller: PWM-Solar Charge Controller
  INA3221 Triple Channel Current/Voltage Monitor Module: INA3221 Triple Channel Current/Voltage Monitor Module Links: INA3221 product information
